// Logisim project RV32I.circ as structural Verilog: 18 circuits, main circuit main
module main (
  output [31:0] AC
);

  wire aselT, brancher_1_brout, bselT, clk, d_ff_1_q, memwenT, not_1_out, not_2_out, or_1_out, PCCtrlT,
       pcwenT, regweT, wbselT;
  wire [1:0] controllogic_1_storesel;
  wire [2:0] brselT, immselT, lselT;
  wire [3:0] controllogic_1_alusel;
  wire [7:0] bitselector_1_out, shifter_1_out;
  wire [31:0] aluctl_1_dataa, aluctl_1_datab, immediategenerator_1_imm_31_0, insT, loadctrl_1_d,
       multiplexer_1_out, multiplexer_2_out, outPCPlus4T, outPCT, rdT, regs_1_rs1, rs2DataT,
       storectrl_1_store_word;

  Clock clock_1 (.out(clk));
  // Probe on insT[11:7]
  // Probe on immselT
  ControlLogic controllogic_1 (
    .ins(insT), .alusel(controllogic_1_alusel), .asel(aselT), .bsel(bselT), .regWe(regweT),
    .imm_sel(immselT), .wbsel(wbselT), .memwen(memwenT), .lsel(lselT), .storesel(controllogic_1_storesel),
    .pcwen(pcwenT), .brsel(brselT));
  regs regs_1 (
    .rsi1(insT[19:15]), .rsi2(insT[24:20]), .rdi(insT[11:7]), .rd(rdT), .clk(clk), .we(regweT),
    .rs1(regs_1_rs1), .rs2(rs2DataT));
  immediateGenerator immediategenerator_1 (.ins(insT), .sel(immselT), .imm_31_0(immediategenerator_1_imm_31_0));
  not not_1 (not_1_out, wbselT);
  not not_2 (not_2_out, PCCtrlT);
  or or_1 (or_1_out, not_1_out, memwenT);
  D_Flip_Flop d_ff_1 (.D(not_2_out), .clk(clk), .Q(d_ff_1_q));  // open: Qn, preset, reset
  brancher brancher_1 (.pcwen(pcwenT), .A(regs_1_rs1), .B(rs2DataT), .brsel(brselT), .brOut(brancher_1_brout));
  Multiplexer #(.width(32)) multiplexer_1 (.in0(outPCT), .in1(AC), .out(multiplexer_1_out), .sel(PCCtrlT));
  BitSelector #(.group(8), .width(32)) bitselector_1 (.in(multiplexer_1_out), .out(bitselector_1_out), .sel(2'b00));
  and and_1 (PCCtrlT, or_1_out, d_ff_1_q);
  Multiplexer #(.width(32)) multiplexer_2 (
    .in0(outPCPlus4T), .in1(AC), .out(multiplexer_2_out), .sel(brancher_1_brout));
  // Probe on aluctl_1_dataa
  ALUCtl aluctl_1 (
    .rs1(regs_1_rs1), .rs2(rs2DataT), .outPC(outPCT), .imm_31_0(immediategenerator_1_imm_31_0), .asel(aselT),
    .bsel(bselT), .dataA(aluctl_1_dataa), .dataB(aluctl_1_datab));
  // Probe on aluctl_1_datab
  // Probe on shifter_1_out
  RAM #(.dataWidth(32)) ram_1 (
    .addr(shifter_1_out), .we(memwenT), .oe(1'b1), .clk(clk), .din(storectrl_1_store_word), .dout(insT));
  Shifter #(.shift("lr")) shifter_1 (.in(bitselector_1_out), .\dist (3'b010), .out(shifter_1_out));
  StoreCtrl storectrl_1 (
    .rs2(rs2DataT), .Address(AC), .storesel(controllogic_1_storesel), .store_word(storectrl_1_store_word));
  pc pc_1 (.clk(clk), .inPC(multiplexer_2_out), .outPCPlus4(outPCPlus4T), .outPC(outPCT));
  alu alu_1 (.A(aluctl_1_dataa), .B(aluctl_1_datab), .sel(controllogic_1_alusel), .AC(AC));
  // Probe on outPCT
  // Probe on insT
  LoadCtrl loadctrl_1 (.Address(AC), .lw(insT), .lsel(lselT), .wbsel(wbselT), .D(loadctrl_1_d));
  Multiplexer #(.width(32)) multiplexer_3 (.in0(loadctrl_1_d), .in1(outPCPlus4T), .out(rdT), .sel(pcwenT));

  // Other names for the same wires on the sheet: ALUT[31:0] = AC; lwT[31:0] = insT; rdiT[4:0] = insT[11:7];
  //   rs1T[4:0] = insT[19:15]; rs2T[4:0] = insT[24:20]

  // Notes on the sheet:
  //   addi x2, x3, 3 - 00318113
  //   jal x1, _test - 004000ef
  //   jal x1, variable - 000100ef
  //   jal x1, _boot - 000000ef
  //   sw x2, 2(x3) - 0021a123
endmodule

module regs (
  input  [4:0] rsi1,
  input  [4:0] rsi2,
  input  [4:0] rdi,
  input  [31:0] rd,
  input  clk,
  input  we,
  output [31:0] rs1,
  output [31:0] rs2
);

  wire x0weT, x1weT, x2weT, x3weT, x4weT, x5weT, x6weT, x7weT, x8weT, x9weT, x10weT, x11weT, x12weT, x13weT,
       x14weT, x15weT, x16weT, x17weT, x18weT, x19weT, x20weT, x21weT, x22weT, x23weT, x24weT, x25weT,
       x26weT, x27weT, x28weT, x29weT, x30weT, x31weT;
  wire [31:0] x1qT, x2qT, x3qT, x4qT, x5qT, x6qT, x7qT, x8qT, x9qT, x10qT, x11qT, x12qT, x13qT, x14qT, x15qT,
       x16qT, x17qT, x18qT, x19qT, x20qT, x21qT, x22qT, x23qT, x24qT, x25qT, x26qT, x27qT, x28qT, x29qT,
       x30qT, x31qT;

  Demultiplexer #(.select(5)) demultiplexer_1 (
    .out0(x0weT), .out1(x1weT), .out2(x2weT), .out3(x3weT), .out4(x4weT), .out5(x5weT), .out6(x6weT),
    .out7(x7weT), .out8(x8weT), .out9(x9weT), .out10(x10weT), .out11(x11weT), .out12(x12weT), .out13(x13weT),
    .out14(x14weT), .out15(x15weT), .out16(x16weT), .out17(x17weT), .out18(x18weT), .out19(x19weT),
    .out20(x20weT), .out21(x21weT), .out22(x22weT), .out23(x23weT), .out24(x24weT), .out25(x25weT),
    .out26(x26weT), .out27(x27weT), .out28(x28weT), .out29(x29weT), .out30(x30weT), .out31(x31weT), .in(we),
    .sel(rdi));
  Register #(.width(32)) x4 (.D(rd), .en(x4weT), .clk(clk), .Q(x4qT));  // open: clr
  Register #(.width(32)) x8 (.D(rd), .en(x8weT), .clk(clk), .Q(x8qT));  // open: clr
  Register #(.width(32)) x12 (.D(rd), .en(x12weT), .clk(clk), .Q(x12qT));  // open: clr
  Register #(.width(32)) x16 (.D(rd), .en(x16weT), .clk(clk), .Q(x16qT));  // open: clr
  Register #(.width(32)) x20 (.D(rd), .en(x20weT), .clk(clk), .Q(x20qT));  // open: clr
  Register #(.width(32)) x24 (.D(rd), .en(x24weT), .clk(clk), .Q(x24qT));  // open: clr
  Register #(.width(32)) x28 (.D(rd), .en(x28weT), .clk(clk), .Q(x28qT));  // open: clr
  Register #(.width(32)) x1 (.D(rd), .en(x1weT), .clk(clk), .Q(x1qT));  // open: clr
  Register #(.width(32)) x5 (.D(rd), .en(x5weT), .clk(clk), .Q(x5qT));  // open: clr
  Register #(.width(32)) x9 (.D(rd), .en(x9weT), .clk(clk), .Q(x9qT));  // open: clr
  Register #(.width(32)) x13 (.D(rd), .en(x13weT), .clk(clk), .Q(x13qT));  // open: clr
  Register #(.width(32)) x17 (.D(rd), .en(x17weT), .clk(clk), .Q(x17qT));  // open: clr
  Register #(.width(32)) x21 (.D(rd), .en(x21weT), .clk(clk), .Q(x21qT));  // open: clr
  Register #(.width(32)) x25 (.D(rd), .en(x25weT), .clk(clk), .Q(x25qT));  // open: clr
  Register #(.width(32)) x29 (.D(rd), .en(x29weT), .clk(clk), .Q(x29qT));  // open: clr
  Register #(.width(32)) x2 (.D(rd), .en(x2weT), .clk(clk), .Q(x2qT));  // open: clr
  Register #(.width(32)) x6 (.D(rd), .en(x6weT), .clk(clk), .Q(x6qT));  // open: clr
  Register #(.width(32)) x10 (.D(rd), .en(x10weT), .clk(clk), .Q(x10qT));  // open: clr
  Register #(.width(32)) x14 (.D(rd), .en(x14weT), .clk(clk), .Q(x14qT));  // open: clr
  Register #(.width(32)) x18 (.D(rd), .en(x18weT), .clk(clk), .Q(x18qT));  // open: clr
  Register #(.width(32)) x22 (.D(rd), .en(x22weT), .clk(clk), .Q(x22qT));  // open: clr
  Register #(.width(32)) x26 (.D(rd), .en(x26weT), .Q(x26qT));  // open: clk, clr
  Register #(.width(32)) x30 (.D(rd), .en(x30weT), .clk(clk), .Q(x30qT));  // open: clr
  Register #(.width(32)) x3 (.D(rd), .en(x3weT), .clk(clk), .Q(x3qT));  // open: clr
  Register #(.width(32)) x15 (.D(rd), .en(x15weT), .clk(clk), .Q(x15qT));  // open: clr
  Register #(.width(32)) x19 (.D(rd), .en(x19weT), .clk(clk), .Q(x19qT));  // open: clr
  Register #(.width(32)) x7 (.D(rd), .en(x7weT), .clk(clk), .Q(x7qT));  // open: clr
  Register #(.width(32)) x11 (.D(rd), .en(x11weT), .clk(clk), .Q(x11qT));  // open: clr
  Register #(.width(32)) x23 (.D(rd), .en(x23weT), .clk(clk), .Q(x23qT));  // open: clr
  Register #(.width(32)) x27 (.D(rd), .en(x27weT), .clk(clk), .Q(x27qT));  // open: clr
  Register #(.width(32)) x31 (.D(rd), .en(x31weT), .clk(clk), .Q(x31qT));  // open: clr
  Multiplexer #(.select(5), .width(32)) multiplexer_1 (
    .in0({32{1'b0}}), .in1(x1qT), .in2(x2qT), .in3(x3qT), .in4(x4qT), .in5(x5qT), .in6(x6qT), .in7(x7qT),
    .in8(x8qT), .in9(x9qT), .in10(x10qT), .in11(x11qT), .in12(x12qT), .in13(x13qT), .in14(x14qT),
    .in15(x15qT), .in16(x16qT), .in17(x17qT), .in18(x18qT), .in19(x19qT), .in20(x20qT), .in21(x21qT),
    .in22(x22qT), .in23(x23qT), .in24(x24qT), .in25(x25qT), .in26(x26qT), .in27(x27qT), .in28(x28qT),
    .in29(x29qT), .in30(x30qT), .in31(x31qT), .out(rs1), .sel(rsi1));
  Multiplexer #(.select(5), .width(32)) multiplexer_2 (
    .in0({32{1'b0}}), .in1(x1qT), .in2(x2qT), .in3(x3qT), .in4(x4qT), .in5(x5qT), .in6(x6qT), .in7(x7qT),
    .in8(x8qT), .in9(x9qT), .in10(x10qT), .in11(x11qT), .in12(x12qT), .in13(x13qT), .in14(x14qT),
    .in15(x15qT), .in16(x16qT), .in17(x17qT), .in18(x18qT), .in19(x19qT), .in20(x20qT), .in21(x21qT),
    .in22(x22qT), .in23(x23qT), .in24(x24qT), .in25(x25qT), .in26(x26qT), .in27(x27qT), .in28(x28qT),
    .in29(x29qT), .in30(x30qT), .in31(x31qT), .out(rs2), .sel(rsi2));

  // Other names for the same wires on the sheet: rdiT[4:0] = rdi; rdT[31:0] = rd; rs1T[31:0] = rs1; rs2T[31:0] = rs2;
  //   rsi1T[4:0] = rsi1; rsi2T[4:0] = rsi2; weT = we
endmodule

module alu (
  input  [31:0] A,
  input  [31:0] B,
  input  [3:0] sel,
  output [31:0] AC
);

  wire comparator_1_lt, comparator_2_lt;
  wire [31:0] addOut, andOut, orOut, sllOut, sltOut, sltuOut, sraOut, srlOut, subOut, xorOut;

  Adder #(.width(32)) adder_1 (.a(A), .b(B), .out(addOut));  // open: cin, cout
  Subtractor #(.width(32)) subtractor_1 (.a(A), .b(B), .out(subOut));  // open: bin, bout
  Shifter #(.width(32)) shifter_1 (.in(A), .\dist (B[4:0]), .out(sllOut));
  Shifter #(.shift("lr"), .width(32)) shifter_2 (.in(A), .\dist (B[4:0]), .out(srlOut));
  Comparator #(.width(32)) comparator_1 (.a(A), .b(B), .lt(comparator_1_lt));  // open: gt, eq
  Comparator #(.mode("unsigned"), .width(32)) comparator_2 (.a(A), .b(B), .lt(comparator_2_lt));  // open: gt, eq
  assign xorOut = A ^ B;  // XOR_Gate xor_1, 32 bits wide
  Shifter #(.shift("ar"), .width(32)) shifter_3 (.in(A), .\dist (B[4:0]), .out(sraOut));
  assign orOut = A | B;  // OR_Gate or_1, 32 bits wide
  assign andOut = A & B;  // AND_Gate and_1, 32 bits wide
  assign sltOut = {{31{1'b0}}, comparator_1_lt};  // Bit_Extender bit_extender_1
  assign sltuOut = {{31{1'b0}}, comparator_2_lt};  // Bit_Extender bit_extender_2
  Multiplexer #(.select(4), .width(32)) multiplexer_1 (
    .in0(addOut), .in1(sllOut), .in2(sltOut), .in3(sltuOut), .in4(xorOut), .in5(srlOut), .in6(orOut),
    .in7(andOut), .in8(subOut), .in13(sraOut), .out(AC), .sel(sel));  // open: in9, in10, in11, in12, in14, in15

  // Other names for the same wires on the sheet: ACT[31:0] = AC; AT[31:0] = A; BT[31:0] = B; selT[3:0] = sel
endmodule

module ISplitter (
  input  [31:0] ins,
  output [6:0] opcode,
  output [4:0] rd,
  output [2:0] funct3,
  output [4:0] rs1,
  output [11:0] imm_11_0
);


  assign funct3 = ins[14:12];
  assign imm_11_0 = ins[31:20];
  assign opcode = ins[6:0];
  assign rd = ins[11:7];
  assign rs1 = ins[19:15];
endmodule

module SSplitter (
  input  [31:0] ins,
  output [6:0] opcode,
  output [4:0] imm_4_0,
  output [2:0] funct3,
  output [4:0] rs1,
  output [4:0] rs2,
  output [6:0] imm_11_5
);


  assign funct3 = ins[14:12];
  assign imm_4_0 = ins[11:7];
  assign imm_11_5 = ins[31:25];
  assign opcode = ins[6:0];
  assign rs1 = ins[19:15];
  assign rs2 = ins[24:20];
endmodule

module USplitter (
  input  [31:0] ins,
  output [6:0] opcode,
  output [4:0] rd,
  output [19:0] imm_31_12
);


  assign imm_31_12 = ins[31:12];
  assign opcode = ins[6:0];
  assign rd = ins[11:7];
endmodule

module BSplitter (
  input  [31:0] ins,
  output [6:0] opcode,
  output imm_11,
  output [3:0] imm_4_1,
  output [2:0] funct3,
  output [4:0] rs1,
  output [4:0] rs2,
  output [5:0] imm_10_5,
  output imm_12
);


  assign funct3 = ins[14:12];
  assign imm_4_1 = ins[11:8];
  assign imm_10_5 = ins[30:25];
  assign imm_11 = ins[7];
  assign imm_12 = ins[31];
  assign opcode = ins[6:0];
  assign rs1 = ins[19:15];
  assign rs2 = ins[24:20];

  // Notes on the sheet:
  //   This is the same as an S Splitter
  //   But we have specific access to the last sign bit
  //   And the MSB of the imm[4:0] field
endmodule

module JSplitter (
  input  [31:0] ins,
  output [6:0] opcode,
  output [4:0] rd,
  output [7:0] imm_19_12,
  output imm_11,
  output [9:0] imm_10_1,
  output imm_20
);


  assign imm_10_1 = ins[30:21];
  assign imm_11 = ins[20];
  assign imm_19_12 = ins[19:12];
  assign imm_20 = ins[31];
  assign opcode = ins[6:0];
  assign rd = ins[11:7];
endmodule

module immediateGenerator (
  input  [31:0] ins,
  input  [2:0] sel,
  output [31:0] imm_31_0
);

  wire imm_11;
  wire [3:0] bsplitter_1_imm_4_1;
  wire [4:0] ssplitter_1_imm_4_0;
  wire [5:0] bsplitter_1_imm_10_5;
  wire [6:0] ssplitter_1_imm_11_5;
  wire [7:0] imm_19_12;
  wire [9:0] imm_10_1;
  wire [11:0] isplitter_1_imm_11_0;
  wire [12:1] bsplitter_1_imm_11;
  wire [20:20] jsplitter_1_imm_20;
  wire [31:0] BOutT, IOutT, JOutT, SOutT;
  wire [31:12] UOutT;

  ISplitter isplitter_1 (.ins(ins), .imm_11_0(isplitter_1_imm_11_0));  // open: opcode, rd, funct3, rs1
  SSplitter ssplitter_1 (
    .ins(ins), .imm_4_0(ssplitter_1_imm_4_0), .imm_11_5(ssplitter_1_imm_11_5));  // open: opcode, funct3, rs1, rs2
  USplitter usplitter_1 (.ins(ins), .imm_31_12(UOutT));  // open: opcode, rd
  BSplitter bsplitter_1 (
    .ins(ins), .imm_11(bsplitter_1_imm_11[1]), .imm_4_1(bsplitter_1_imm_4_1),
    .imm_10_5(bsplitter_1_imm_10_5), .imm_12(bsplitter_1_imm_11[12]));  // open: opcode, funct3, rs1, rs2
  JSplitter jsplitter_1 (
    .ins(ins), .imm_19_12(imm_19_12), .imm_11(imm_11), .imm_10_1(imm_10_1), .imm_20(jsplitter_1_imm_20[20]));  // open: opcode, rd
  assign IOutT = {{20{isplitter_1_imm_11_0[11]}}, isplitter_1_imm_11_0};  // Bit_Extender bit_extender_1
  assign SOutT = {{20{ssplitter_1_imm_11_5[6]}}, {ssplitter_1_imm_11_5, ssplitter_1_imm_4_0}};  // Bit_Extender bit_extender_2
  assign BOutT = {{19{bsplitter_1_imm_11[12]}}, {bsplitter_1_imm_11[12], bsplitter_1_imm_10_5, bsplitter_1_imm_4_1, bsplitter_1_imm_11[1], 1'b0}};  // Bit_Extender bit_extender_3
  assign JOutT = {{11{jsplitter_1_imm_20[20]}}, {jsplitter_1_imm_20[20], imm_19_12, imm_11, imm_10_1, 1'b0}};  // Bit_Extender bit_extender_4
  Multiplexer #(.select(3), .width(32)) multiplexer_1 (
    .in0(IOutT), .in1(SOutT), .in2(BOutT), .in3(JOutT), .in4({UOutT, {12{1'b0}}}), .out(imm_31_0), .sel(sel));  // open: in5, in6, in7

  // Other names for the same wires on the sheet: insT[31:0] = ins; selT[2:0] = sel
endmodule

module brancher (
  input  pcwen,
  input  [31:0] A,
  input  [31:0] B,
  input  [2:0] brsel,
  output brOut
);

  wire comparator_1_eq, comparator_1_gt, comparator_1_lt, comparator_2_eq, comparator_2_gt, comparator_2_lt,
       multiplexer_1_out, not_1_out, or_1_out, or_2_out;

  Comparator #(.width(32)) comparator_1 (
    .a(A), .b(B), .gt(comparator_1_gt), .eq(comparator_1_eq), .lt(comparator_1_lt));
  Comparator #(.mode("unsigned"), .width(32)) comparator_2 (
    .a(A), .b(B), .gt(comparator_2_gt), .eq(comparator_2_eq), .lt(comparator_2_lt));
  or or_1 (or_1_out, comparator_1_gt, comparator_1_eq);
  or or_2 (or_2_out, comparator_2_gt, comparator_2_eq);
  not not_1 (not_1_out, comparator_1_eq);
  Multiplexer #(.select(3)) multiplexer_1 (
    .in0(comparator_1_eq), .in1(not_1_out), .in3(1'b1), .in4(comparator_1_lt), .in5(or_1_out),
    .in6(or_2_out), .in7(comparator_2_lt), .out(multiplexer_1_out), .sel(brsel));  // open: in2
  and and_1 (brOut, multiplexer_1_out, pcwen);

  // Other names for the same wires on the sheet: AT[31:0] = A; brselT[2:0] = brsel; BT[31:0] = B; pcwenT = pcwen

  // Notes on the sheet:
  //   Use unsigned branching flag
endmodule

module pc (
  input  clk,
  input  [31:0] inPC,
  output [31:0] outPCPlus4,
  output [31:0] outPC
);

  Register #(.width(32)) register_1 (.D(inPC), .clk(clk), .Q(outPC));  // open: en, clr
  Adder #(.width(32)) adder_1 (.a(outPC), .b(32'h4), .out(outPCPlus4));  // open: cin, cout

  // Other names for the same wires on the sheet: inPCT[31:0] = inPC; outPCPlus4T[31:0] = outPCPlus4;
  //   outPCT[31:0] = outPC
endmodule

module RSplitter (
  input  [31:0] ins,
  output [6:0] opcode,
  output [4:0] rd,
  output [2:0] funct3,
  output [4:0] rs1,
  output [4:0] rs2,
  output [6:0] funct7
);


  assign funct3 = ins[14:12];
  assign funct7 = ins[31:25];
  assign opcode = ins[6:0];
  assign rd = ins[11:7];
  assign rs1 = ins[19:15];
  assign rs2 = ins[24:20];
endmodule

module ControlLogic (
  input  [31:0] ins,
  output [3:0] alusel,
  output asel,
  output bsel,
  output regWe,
  output [2:0] imm_sel,
  output wbsel,
  output memwen,
  output [2:0] lsel,
  output [1:0] storesel,
  output pcwen,
  output [2:0] brsel
);

  ROM #(.addrWidth(9), .dataWidth(21)) rom_1 (
    .addr({ins[30], ins[14:12], ins[6:2]}),
    .data({brsel, pcwen, storesel, memwen, lsel, wbsel, alusel, regWe, imm_sel, bsel, asel}));

  // Other names for the same wires on the sheet: b2T = ins[2]; b3T = ins[3]; b4T = ins[4]; b5T = ins[5]; b6T = ins[6];
  //   b12T = ins[12]; b13T = ins[13]; b14T = ins[14]; b30T = ins[30]; aselT = asel; bselT = bsel; regWeT = regWe;
  //   wbselT = wbsel; memwenT = memwen; pcwenT = pcwen; brsel0T = brsel[0]; brsel1T = brsel[1]; brsel2T = brsel[2];
  //   is0T = imm_sel[0]; is1T = imm_sel[1]; is2T = imm_sel[2]; lsel0T = lsel[0]; lsel1T = lsel[1]; lsel2T = lsel[2];
  //   storesel0T = storesel[0]; storesel1T = storesel[1]

  // Notes on the sheet:
  //   contents of rom_1 (hex, n*v repeats v):
  //   c0022 0 0 0 c0422 0 0 0 c4406 0 0 0 c0420 11*0 2040b e0422 0 e042f 4*0 c0822 0 0 0 c0462 0 0 0 cc406
  //   0 0 0 c0460 11*0 6000b 7*0 c1022 0 0 0 c04a2 0 0 0 d4406 0 0 0 c04a0 23*0 c04e2 7*0 c04e0 19*0 c2022
  //   0 0 0 c0522 7*0 c0520 11*0 12000b 7*0 c2822 0 0 0 c0562 7*0 c0560 11*0 16000b 11*0 c05a2 7*0 c05a0
  //   11*0 1a000b 11*0 c05e2 7*0 c05e0 11*0 1e000b 19*0 c0620 151*0 c0762 7*0 c0760
endmodule

module ALUCtl (
  input  [31:0] rs1,
  input  [31:0] rs2,
  input  [31:0] outPC,
  input  [31:0] imm_31_0,
  input  asel,
  input  bsel,
  output [31:0] dataA,
  output [31:0] dataB
);

  Multiplexer #(.width(32)) multiplexer_1 (.in0(rs2), .in1(imm_31_0), .out(dataB), .sel(bsel));
  Multiplexer #(.width(32)) multiplexer_2 (.in0(rs1), .in1(outPC), .out(dataA), .sel(asel));

  // Other names for the same wires on the sheet: imm_31_0T[31:0] = imm_31_0; outPCT[31:0] = outPC; rs1T[31:0] = rs1;
  //   rs2T[31:0] = rs2
endmodule

module LoadByte (
  input  [31:0] Address,
  input  [31:0] load_word,
  output [31:0] lb,
  output [31:0] lbu
);

  wire [4:0] bitselector_1_out;
  wire [7:0] bitselector_2_out;
  wire [31:0] and_1_out, shifter_1_out, ShiftT, subtractor_1_out;

  BitSelector #(.group(5), .width(32)) bitselector_1 (.in(ShiftT), .out(bitselector_1_out), .sel(3'b000));
  assign and_1_out = Address & 32'h3;  // AND_Gate and_1, 32 bits wide
  // Probe on and_1_out
  // Probe on shifter_1_out
  Shifter #(.shift("lr"), .width(32)) shifter_1 (.in(load_word), .\dist (bitselector_1_out), .out(shifter_1_out));
  // Probe on subtractor_1_out
  Subtractor #(.width(32)) subtractor_1 (.a(32'h3), .b(and_1_out), .out(subtractor_1_out));  // open: bin, bout
  // Probe on ShiftT
  Shifter #(.width(32)) shifter_2 (.in(subtractor_1_out), .\dist (5'b00011), .out(ShiftT));
  // Probe on lbu
  assign lbu = shifter_1_out & 32'hff;  // AND_Gate and_2, 32 bits wide
  BitSelector #(.group(8), .width(32)) bitselector_2 (.in(shifter_1_out), .out(bitselector_2_out), .sel(2'b00));
  assign lb = {{24{bitselector_2_out[7]}}, bitselector_2_out};  // Bit_Extender bit_extender_1

  // Other names for the same wires on the sheet: AddressT[31:0] = Address; lbT[31:0] = lb; lbuT[31:0] = lbu;
  //   lwT[31:0] = load_word
endmodule

module LoadHalfWord (
  input  [31:0] Address,
  input  [31:0] load_word,
  output [31:0] lh,
  output [31:0] lhu
);

  wire bitselector_1_out, not_1_out;
  wire [15:0] bitselector_2_out;

  BitSelector #(.width(32)) bitselector_1 (.in(Address), .out(bitselector_1_out), .sel(5'b00001));
  BitSelector #(.group(16), .width(32)) bitselector_2 (.in(load_word), .out(bitselector_2_out), .sel(not_1_out));
  not not_1 (not_1_out, bitselector_1_out);
  // Probe on bitselector_2_out
  assign lh = {{16{bitselector_2_out[15]}}, bitselector_2_out};  // Bit_Extender bit_extender_1
  assign lhu = {{16{1'b0}}, bitselector_2_out};  // Bit_Extender bit_extender_2

  // Other names for the same wires on the sheet: AddressT[31:0] = Address; lhT[31:0] = lh; lhuT[31:0] = lhu;
  //   lwT[31:0] = load_word
endmodule

module LoadCtrl (
  input  [31:0] Address,
  input  [31:0] lw,
  input  [2:0] lsel,
  input  wbsel,
  output [31:0] D
);

  wire [31:0] lbT, lbuT, lhT, lhuT, multiplexer_1_out;

  LoadByte loadbyte_1 (.Address(Address), .load_word(lw), .lb(lbT), .lbu(lbuT));
  Multiplexer #(.select(3), .width(32)) multiplexer_1 (
    .in0(lbT), .in1(lhT), .in2(lw), .in4(lbuT), .in5(lhuT), .out(multiplexer_1_out), .sel(lsel));  // open: in3, in6, in7
  LoadHalfWord loadhalfword_1 (.Address(Address), .load_word(lw), .lh(lhT), .lhu(lhuT));
  Multiplexer #(.width(32)) multiplexer_2 (.in0(multiplexer_1_out), .in1(Address), .out(D), .sel(wbsel));

  // Other names for the same wires on the sheet: AddressT[31:0] = Address; dT[31:0] = D; lselT[2:0] = lsel;
  //   lwT[31:0] = lw; wbselT = wbsel

  // Notes on the sheet:
  //   Load Controller
endmodule

module StoreCtrl (
  input  [31:0] rs2,
  input  [31:0] Address,
  input  [1:0] storesel,
  output [31:0] store_word
);

  wire bitselector_2_out, not_1_out;
  wire [4:0] bitselector_1_out;
  wire [7:0] bitselector_4_out;
  wire [15:0] bitselector_3_out;
  wire [31:0] and_1_out, sbT, shifter_1_out, ShiftT, shT, subtractor_1_out;

  BitSelector #(.group(5), .width(32)) bitselector_1 (.in(ShiftT), .out(bitselector_1_out), .sel(3'b000));
  assign and_1_out = Address & 32'h3;  // AND_Gate and_1, 32 bits wide
  BitSelector #(.width(32)) bitselector_2 (.in(Address), .out(bitselector_2_out), .sel(5'b00001));
  // Probe on and_1_out
  Shifter #(.shift("lr"), .width(32)) shifter_1 (.in(rs2), .\dist (bitselector_1_out), .out(shifter_1_out));
  BitSelector #(.group(16), .width(32)) bitselector_3 (.in(rs2), .out(bitselector_3_out), .sel(not_1_out));
  not not_1 (not_1_out, bitselector_2_out);
  // Probe on shifter_1_out
  // Probe on bitselector_3_out
  Subtractor #(.width(32)) subtractor_1 (.a(32'h3), .b(and_1_out), .out(subtractor_1_out));  // open: bin, bout
  assign shT = {{16{bitselector_3_out[15]}}, bitselector_3_out};  // Bit_Extender bit_extender_1
  // Probe on subtractor_1_out
  BitSelector #(.group(8), .width(32)) bitselector_4 (.in(shifter_1_out), .out(bitselector_4_out), .sel(2'b00));
  // Probe on ShiftT
  Shifter #(.width(32)) shifter_2 (.in(subtractor_1_out), .\dist (5'b00011), .out(ShiftT));
  assign sbT = {{24{bitselector_4_out[7]}}, bitselector_4_out};  // Bit_Extender bit_extender_2
  Multiplexer #(.select(2), .width(32)) multiplexer_1 (
    .in0(sbT), .in1(shT), .in2(rs2), .out(store_word), .sel(storesel));  // open: in3

  // Other names for the same wires on the sheet: addressT[31:0] = Address; rs2T[31:0] = rs2
endmodule
